# Fritzing sketch grow plant project pcb (saved by Fritzing 0.9.10b)

parts:
  Part1 = Arduino Nano (Rev3.0)
  LDR_SENSOR = Photocell (LDR) [package=THT]
  SWITCH = SWITCH-SPST-2 [package=switch-spst-vertical]
  BATTERY = LIPO-2000mAh [package=lipo-2000]
  capacitive_touch_sensor = CAPSENSE_PAD [package=capsense_pad]
  OLED = Grove 3 Axis Digital Accelerometer 16g

nets:
  GND: Part1.GND, LDR_SENSOR.pin_1, OLED.GND
  N1: Part1.D2, LDR_SENSOR.pin_0
  N2: Part1.D3, capacitive_touch_sensor.RECEIVE
  N3: Part1.A5, OLED.SCL
  N4: Part1.A4, OLED.SDA
  SOIL MOISTURE SENSOR: Part1.A0
  N5: SWITCH.P, BATTERY.-
  N6: BATTERY.+, OLED.VCC

notes:
  connect scl to A4
  connect sdk to A5
  of oled display if don,t work flip the pin
  CONNECT SIGNAL PIN TO THE ARDUINO pin from the moister sensor
